# Fritzing sketch audioamp (saved by Fritzing 0.9.6b)
breadboards: 1

parts:
  R1 = Resistor [tolerance=±5% resistance=100 package=THT]
  S8050 = PNP-Transistor [package="TO92 [THT]"]
  C1 = Electrolytic Capacitor [capacitance=10µF voltage=50V package="100 mil [THT, electrolytic]"]
  R2 = Resistor [tolerance=±5% resistance=20 package=THT]
  R4 = Resistor [tolerance=±5% resistance=1k package=THT]
  R3 = Resistor [tolerance=±5% resistance=3220 package=THT]
  C2 = Electrolytic Capacitor [capacitance=10µF voltage=50V package="100 mil [THT, electrolytic]"]
  8_ohm_speaker = SPEAKER [package=pcb_mount_speaker]
  Audio_Jack/signal = 3.5mm Audio Jack [package=audio-jack-3.5mm-smd]

nets:
  5V: R1.Pin_0, R3.Pin_0
  N1: R1.Pin_1, S8050.E, C1.-
  N2: S8050.B, R4.Pin_0, R3.Pin_1, C2.+
  N3: S8050.C, R2.Pin_0
  N4: C1.+, 8_ohm_speaker.+
  GND: R2.Pin_1, R4.Pin_1, 8_ohm_speaker.-, Audio_Jack/signal.SLEEVE
  N5: C2.-, Audio_Jack/signal.RIGHT
